// Logisim project C-6bitDemultiplexer.circ as structural Verilog: 1 circuit, main circuit 6bitDemultiplexer
module _6bitDemultiplexer (
  input  Power,
  input  [5:0] _6bit_Selector,
  output Output_0,
  output Output_1,
  output Output_2,
  output Output_3,
  output Output_4,
  output Output_5,
  output Output_6,
  output Output_7,
  output Output_8,
  output Output_9,
  output Output_10,
  output Output_11,
  output Output_12,
  output Output_13,
  output Output_14,
  output Output_15,
  output Output_16,
  output Output_17,
  output Output_18,
  output Output_19,
  output Output_20,
  output Output_21,
  output Output_22,
  output Output_23,
  output Output_24,
  output Output_25,
  output Output_26,
  output Output_27,
  output Output_28,
  output Output_29,
  output Output_30,
  output Output_31,
  output Output_32,
  output Output_33,
  output Output_34,
  output Output_35,
  output Output_36,
  output Output_37,
  output Output_38,
  output Output_39,
  output Output_40,
  output Output_41,
  output Output_42,
  output Output_43,
  output Output_44,
  output Output_45,
  output Output_46,
  output Output_47,
  output Output_48,
  output Output_49,
  output Output_50,
  output Output_51,
  output Output_52,
  output Output_53,
  output Output_54,
  output Output_55,
  output Output_56,
  output Output_57,
  output Output_58,
  output Output_59,
  output Output_60,
  output Output_61,
  output Output_62,
  output Output_63
);

  wire multiplexer_1_out, multiplexer_2_out;

  Multiplexer #(.enable("false")) multiplexer_1 (
    .in0(Power), .in1(1'b0), .out(multiplexer_1_out), .sel(_6bit_Selector[5]));
  Multiplexer #(.enable("false")) multiplexer_2 (
    .in0(1'b0), .in1(Power), .out(multiplexer_2_out), .sel(_6bit_Selector[5]));
  Demultiplexer #(.select(5), .enable("false")) demultiplexer_1 (
    .out0(Output_0), .out1(Output_1), .out2(Output_2), .out3(Output_3), .out4(Output_4), .out5(Output_5),
    .out6(Output_6), .out7(Output_7), .out8(Output_8), .out9(Output_9), .out10(Output_10), .out11(Output_11),
    .out12(Output_12), .out13(Output_13), .out14(Output_14), .out15(Output_15), .out16(Output_16),
    .out17(Output_17), .out18(Output_18), .out19(Output_19), .out20(Output_20), .out21(Output_21),
    .out22(Output_22), .out23(Output_23), .out24(Output_24), .out25(Output_25), .out26(Output_26),
    .out27(Output_27), .out28(Output_28), .out29(Output_29), .out30(Output_30), .out31(Output_31),
    .in(multiplexer_1_out), .sel(_6bit_Selector[4:0]));
  Demultiplexer #(.select(5), .enable("false")) demultiplexer_2 (
    .out0(Output_32), .out1(Output_33), .out2(Output_34), .out3(Output_35), .out4(Output_36),
    .out5(Output_37), .out6(Output_38), .out7(Output_39), .out8(Output_40), .out9(Output_41),
    .out10(Output_42), .out11(Output_43), .out12(Output_44), .out13(Output_45), .out14(Output_46),
    .out15(Output_47), .out16(Output_48), .out17(Output_49), .out18(Output_50), .out19(Output_51),
    .out20(Output_52), .out21(Output_53), .out22(Output_54), .out23(Output_55), .out24(Output_56),
    .out25(Output_57), .out26(Output_58), .out27(Output_59), .out28(Output_60), .out29(Output_61),
    .out30(Output_62), .out31(Output_63), .in(multiplexer_2_out), .sel(_6bit_Selector[4:0]));

  // Other names for the same wires on the sheet: Selector[4:0] = _6bit_Selector[4:0]; TOP_BIT = _6bit_Selector[5]
endmodule
