// Logisim project C-ALU.circ as structural Verilog: 4 circuits, main circuit ALU
module ALU (
  input  [31:0] in_1,
  input  [31:0] in_2,
  input  [3:0] in_3,
  output [31:0] out_4,
  output [31:0] out_5,
  output [31:0] out_6,
  output ZeroFlag,
  output NegativeFlag
);

  wire comparator_1_eq, comparator_2_eq, comparator_4_lt, comparator_5_lt, enable, UNSIGNED;
  wire [31:0] add, \and , div, multHi, multLo, \nor , \or , rem, slt, sltu, sub, \xor ;

  Adder #(.width(32)) adder_1 (.a(in_1), .b(in_2), .out(add));  // open: cin, cout
  Subtractor #(.width(32)) subtractor_1 (.a(in_1), .b(in_2), .out(sub));  // open: bin, bout
  Comparator #(.width(4)) comparator_1 (.a(4'b0101), .b(in_3), .eq(comparator_1_eq));  // open: gt, lt
  Comparator #(.width(4)) comparator_2 (.a(in_3), .b(4'b0111), .eq(comparator_2_eq));  // open: gt, lt
  Multiplexer #(.select(4), .width(32), .enable("false")) multiplexer_1 (
    .in0(add), .in1(sub), .in2(slt), .in3(sltu), .in4({32{1'b0}}), .in5({32{1'b0}}), .in6({32{1'b0}}),
    .in7({32{1'b0}}), .in8(\and ), .in9(\or ), .in10(\nor ), .in11(\xor ), .out(out_4), .sel(in_3));  // open: in12, in13, in14, in15
  MULTIPLIER multiplier_1 (.A(in_1), .B(in_2), .\unsigned (UNSIGNED), .LO(multLo), .HI(multHi));
  DIVIDER divider_1 (.A(in_1), .B(in_2), .in_3(UNSIGNED), .QUOTIENT(div), .REMAINDER(rem));
  or or_1 (UNSIGNED, comparator_1_eq, comparator_2_eq);
  assign \and  = in_1 & in_2;  // AND_Gate and_1, 32 bits wide
  assign \or  = in_1 | in_2;  // OR_Gate or_2, 32 bits wide
  assign \nor  = ~(in_1 | in_2);  // NOR_Gate nor_1, 32 bits wide
  assign \xor  = in_1 ^ in_2;  // XOR_Gate xor_1, 32 bits wide
  Comparator #(.width(2)) comparator_3 (.a(in_3[3:2]), .b(2'b01), .eq(enable));  // open: gt, lt
  Comparator #(.width(32)) comparator_4 (.a(in_1), .b(in_2), .lt(comparator_4_lt));  // open: gt, eq
  Comparator #(.width(32), .mode("unsigned")) comparator_5 (.a(in_1), .b(in_2), .lt(comparator_5_lt));  // open: gt, eq
  Multiplexer #(.width(32), .enable("false")) multiplexer_2 (
    .in0({32{1'b0}}), .in1(32'h1), .out(slt), .sel(comparator_4_lt));
  Multiplexer #(.width(32), .enable("false")) multiplexer_3 (
    .in0({32{1'b0}}), .in1(32'h1), .out(sltu), .sel(comparator_5_lt));
  Multiplexer #(.select(2), .width(32)) multiplexer_4 (
    .in0(multLo), .in1(multLo), .in2(div), .in3(div), .out(out_5), .sel(in_3[1:0]), .en(enable));
  Comparator #(.width(32)) comparator_6 (.a(out_4), .b({32{1'b0}}), .eq(ZeroFlag), .lt(NegativeFlag));  // open: gt
  Multiplexer #(.select(2), .width(32)) multiplexer_5 (
    .in0(multHi), .in1(multHi), .in2(rem), .in3(rem), .out(out_6), .sel(in_3[1:0]), .en(enable));

  // Other names for the same wires on the sheet: A[31:0] = in_1; B[31:0] = in_2; High[31:0] = out_6;
  //   Low[31:0] = out_5; opcode[3:0] = in_3; oplo[1:0] = in_3[1:0]; ophi[1:0] = in_3[3:2]; result[31:0] = out_4

  // Notes on the sheet:
  //   Operaciones
  //   Add    0
  //   Sub    1
  //   Slt    2
  //   Sltu    3
  //   Mult    4  0100
  //   Multu    5 0101
  //   Div    6 0110
  //   Divu    7 0111
  //   Determinar si se efectua una operacion que modifica el low o el high (01 high order bits)
  //   Opcodes
  //   And    8
  //   Or    9
  //   Nor   10
  //   Xor   11
  //   Flags
endmodule

module MULTIPLIER (
  input  [31:0] A,
  input  [31:0] B,
  input  \unsigned ,
  output [31:0] LO,
  output [31:0] HI
);

  wire adder_1_cout, sel, sigA, sigB, xor_1_out;
  wire [31:0] absA, absB, bit_extender_1_out, HI_t, LO_t, not_1_out, not_2_out, SHI, SLO;

  ABS abs_1 (.A(A), .UNSIGNED(\unsigned ), .SIGN(sigA), .ABS_A(absA));
  Multiplier #(.width(32)) multiplier_1 (.a(absA), .b(absB), .out(LO_t), .cout(HI_t));  // open: cin
  and and_1 (sel, ~\unsigned , xor_1_out);  // AND_Gate
  xor xor_1 (xor_1_out, sigA, sigB);
  ABS abs_2 (.A(B), .UNSIGNED(\unsigned ), .SIGN(sigB), .ABS_A(absB));
  Multiplexer #(.width(32)) multiplexer_1 (.in0(LO_t), .in1(SLO), .out(LO), .sel(sel));  // open: en
  Multiplexer #(.width(32)) multiplexer_2 (.in0(HI_t), .in1(SHI), .out(HI), .sel(sel));  // open: en
  assign not_1_out = ~LO_t;  // NOT_Gate not_1, 32 bits wide
  Adder #(.width(32)) adder_1 (.a(not_1_out), .b(32'h1), .out(SLO), .cout(adder_1_cout));  // open: cin
  assign not_2_out = ~HI_t;  // NOT_Gate not_2, 32 bits wide
  assign bit_extender_1_out = {{31{1'b0}}, adder_1_cout};  // Bit_Extender bit_extender_1
  Adder #(.width(32)) adder_2 (.a(not_2_out), .b(bit_extender_1_out), .out(SHI));  // open: cin, cout

  // Other names for the same wires on the sheet: FHI[31:0] = HI; FLO[31:0] = LO
endmodule

module DIVIDER (
  input  [31:0] A,
  input  [31:0] B,
  input  in_3,
  output [31:0] QUOTIENT,
  output [31:0] REMAINDER
);

  wire negA, negB, negO, sigA, sigB;
  wire [31:0] absA, absB, adder_1_out, divider_1_out, multiplexer_2_out, negator_1_out, R, subtractor_1_out;

  ABS abs_1 (.A(A), .UNSIGNED(in_3), .SIGN(sigA), .ABS_A(absA));
  Divider #(.width(32)) divider_1 (.a(absA), .b(absB), .out(divider_1_out), .rem(R));  // open: upper
  Subtractor #(.width(32)) subtractor_1 (.a(absB), .b(R), .out(subtractor_1_out));  // open: bin, bout
  ABS abs_2 (.A(B), .UNSIGNED(in_3), .SIGN(sigB), .ABS_A(absB));
  Adder #(.width(32)) adder_1 (.a(divider_1_out), .b(32'h1), .out(adder_1_out));  // open: cin, cout
  Multiplexer #(.width(32)) multiplexer_1 (.in0(R), .in1(subtractor_1_out), .out(REMAINDER), .sel(negA));  // open: en
  Multiplexer #(.width(32)) multiplexer_2 (
    .in0(divider_1_out), .in1(adder_1_out), .out(multiplexer_2_out), .sel(negA));  // open: en
  Negator #(.width(32)) negator_1 (.in(multiplexer_2_out), .out(negator_1_out));
  Multiplexer #(.width(32)) multiplexer_3 (
    .in0(multiplexer_2_out), .in1(negator_1_out), .out(QUOTIENT), .sel(negO));  // open: en
  and and_1 (negA, sigA, ~in_3);  // AND_Gate
  and and_2 (negB, ~in_3, sigB);  // AND_Gate
  xor xor_1 (negO, negA, negB);

  // Other names for the same wires on the sheet: unsigned = in_3
endmodule

module ABS (
  input  [31:0] A,
  input  UNSIGNED,
  output [31:0] ABS_A,
  output SIGN
);

  wire and_1_out;
  wire [31:0] negator_1_out;

  Multiplexer #(.width(32)) multiplexer_1 (.in0(A), .in1(negator_1_out), .out(ABS_A), .sel(and_1_out));  // open: en
  Negator #(.width(32)) negator_1 (.in(A), .out(negator_1_out));
  and and_1 (and_1_out, A[31], ~UNSIGNED);  // AND_Gate

  assign SIGN = A[31];

  // Other names for the same wires on the sheet: bit31 = A[31]
endmodule
