// Logisim project C-BranchControl.circ as structural Verilog: 1 circuit, main circuit BranchControl
module BranchControl (
  input  [31:0] Instruction_Address,
  output [31:0] Next_Instruction_Address
);


  assign Next_Instruction_Address = Instruction_Address;
endmodule
