// Logisim project C-DataPath.circ as structural Verilog: 1 circuit, main circuit DataPath
module DataPath (
  input  in_1,
  input  [31:0] Next_Instruction_Address,
  input  in_3,
  input  in_4,
  input  in_5,
  input  [31:0] in_6,
  output [31:0] Program_Counter,
  output [4:0] RS,
  output [31:0] const_ext,
  output [5:0] CODE
);

  wire [31:0] IR;

  Register #(.width(32)) u_Program_Counter (
    .D(Next_Instruction_Address), .en(in_4), .Q(Program_Counter), .clk(in_3), .clr(in_1));
  InstructionDecoder instructiondecoder_1 (
    .Instruccion(IR), .Rs(RS), .CODE(CODE), .ConstanteExtendida(const_ext));  // open: OPCODE, FUNCODE, Rt, Rd, Constante, Destino_Salto
  Register #(.width(32)) Instruction_Register (.D(in_6), .en(in_5), .Q(IR), .clk(in_3), .clr(in_1));

  // Other names for the same wires on the sheet: CLK = in_3; FetchedInstruction[31:0] = in_6; LoadIR = in_5;
  //   LoadPC = in_4; RST = in_1

  // Notes on the sheet:
  //   For control unit
endmodule
