// Logisim project C-EndiannesConverter.circ as structural Verilog: 2 circuits, main circuit LittleToBigEndian
module LittleToBigEndian (
  input  [31:0] in_1,
  output [31:0] out_2
);


  assign out_2 = {in_1[7:0], in_1[15:8], in_1[23:16], in_1[31:24]};
endmodule

module BigToLittleEndian (
  input  [31:0] in_1,
  output [31:0] out_2
);


  assign out_2 = {in_1[7:0], in_1[15:8], in_1[23:16], in_1[31:24]};
endmodule
