// Logisim project C-FetchInstruction.circ as structural Verilog: 1 circuit, main circuit FetchInstruction
module FetchInstruction (
  input  [31:0] Program_Counter_Address,
  input  [31:0] Ram_out_0,
  input  [31:0] Ram_out_1,
  input  [31:0] Ram_out_2,
  input  [31:0] Ram_out_3,
  input  [3:0] Read_Time,
  input  CONTROL_SIGNALS,
  input  in_8,
  input  in_9,
  output [15:0] Address,
  output Instruction_Ready,
  output [31:0] Instruction,
  output Chip_Select,
  output Read_Write,
  output out_15
);

  wire CS0, d_ff_1_q, d_ff_2_q, demultiplexer_1_out0, demultiplexer_1_out1, demultiplexer_2_out0, MATCH,
       or_1_out, RST_Count;
  wire [3:0] counter_1_q;
  wire [31:0] RAM_OUT_0_t, RAM_OUT_1_t, RAM_OUT_2_t, RAM_OUT_3_t;

  LittleToBigEndian littletobigendian_1 (.in_1(Ram_out_0), .out_2(RAM_OUT_0_t));
  LittleToBigEndian littletobigendian_2 (.in_1(Ram_out_1), .out_2(RAM_OUT_1_t));
  LittleToBigEndian littletobigendian_3 (.in_1(Ram_out_2), .out_2(RAM_OUT_2_t));
  LittleToBigEndian littletobigendian_4 (.in_1(Ram_out_3), .out_2(RAM_OUT_3_t));
  D_Flip_Flop d_ff_1 (.clk(CONTROL_SIGNALS), .D(or_1_out), .Q(d_ff_1_q), .preset(in_8));  // open: Qn, en, reset
  or or_1 (or_1_out, demultiplexer_1_out0, out_15);
  Demultiplexer #(.enable("false")) demultiplexer_1 (
    .out0(demultiplexer_1_out0), .out1(demultiplexer_1_out1), .in(d_ff_1_q), .sel(in_9));
  or or_2 (CS0, demultiplexer_2_out0, demultiplexer_1_out1);
  D_Flip_Flop d_ff_2 (.clk(CONTROL_SIGNALS), .D(CS0), .Q(d_ff_2_q), .reset(in_8));  // open: Qn, preset, en
  Multiplexer #(.select(2), .width(32), .enable("false")) multiplexer_1 (
    .in0(RAM_OUT_0_t), .in1(RAM_OUT_1_t), .in2(RAM_OUT_2_t), .in3(RAM_OUT_3_t), .out(Instruction),
    .sel(Program_Counter_Address[3:2]));
  Demultiplexer #(.enable("false")) demultiplexer_2 (
    .out0(demultiplexer_2_out0), .out1(Instruction_Ready), .in(d_ff_2_q), .sel(MATCH));
  or or_3 (RST_Count, in_8, out_15);
  Counter #(.width(4), .max('hf)) counter_1 (
    .Q(counter_1_q), .clk(CONTROL_SIGNALS), .clr(RST_Count));  // open: load, D, count, carry
  or or_4 (Chip_Select, CS0, Instruction_Ready);
  Comparator #(.width(4)) comparator_1 (.a(Read_Time), .b(counter_1_q), .eq(MATCH));  // open: gt, lt
  D_Flip_Flop Wait_for_the_data_path_to_store_the_instruction (
    .clk(CONTROL_SIGNALS), .D(Instruction_Ready), .Q(out_15), .reset(in_8));  // open: Qn, preset, en

  assign Address = Program_Counter_Address[19:4];
  assign Read_Write = 1'b0;

  // Other names for the same wires on the sheet: CLK = CONTROL_SIGNALS; CS = Chip_Select; END = out_15;
  //   OFFSET[1:0] = Program_Counter_Address[3:2]; LINEA[15:0] = Program_Counter_Address[19:4];
  //   CS1 = Instruction_Ready; Ready = Instruction_Ready; RST = in_8; START = in_9

  // Notes on the sheet:
  //   RAM TIMING
  //   RAM CONTROL
  //   Los primeros
  //   20 bits de la direccion
  //   son los que interesan
  //   RAM ADDRESS
  //   DATA FROM RAM
  //   LINEA
  //   Los 16 bits mas significativos
  //   dan la linea que contiene la direccion
  //   Bytes direccionables = lineas * bytes por linea
  //   2^20 = 2^16 * 2^4
  //   linea de memoria = direccion / 16
  //   OFFSET
  //   LINEA
  //   Los 4 bits menos significativos
  //   dan el byte especifico en la linea
  //   al que apunta la direccion
  //   Los dos bits mas significativos
  //   representan el bloque de 4 bytes al que pertenece
  //   la direccion en la linea
  //   MINI DATA PATH
  //   Instruction
  //   on the cable
endmodule
