// Logisim project C-InstructionDecoder.circ as structural Verilog: 1 circuit, main circuit InstructionDecoder
module InstructionDecoder (
  input  [31:0] Instruccion,
  output [5:0] OPCODE,
  output [5:0] FUNCODE,
  output [4:0] Rs,
  output [4:0] Rt,
  output [4:0] Rd,
  output [15:0] Constante,
  output [25:0] Destino_Salto,
  output [31:0] ConstanteExtendida,
  output [31:0] _4_offset,
  output [5:0] CODE
);

  wire and_1_out, and_2_out, and_3_out, and_4_out, and_5_out, and_6_out, and_7_out, and_8_out, and_10_out,
       and_11_out, and_12_out, and_13_out, and_14_out, and_15_out, and_16_out, nf0, nf1, nf2, nf3, nf4, nf5,
       not_13_out, not_14_out, not_15_out, not_16_out, not_17_out, np0, np1, np2, np3, np4, np5, or_1_out,
       or_5_out;
  wire [2:0] CodeSelector;
  wire [5:0] or_2_out, or_3_out;

  not not_1 (np0, Instruccion[26]);
  not not_2 (np1, Instruccion[27]);
  not not_3 (np2, Instruccion[28]);
  not not_4 (np3, Instruccion[29]);
  not not_5 (np4, Instruccion[30]);
  not not_6 (np5, Instruccion[31]);
  not not_7 (nf0, Instruccion[0]);
  not not_8 (nf1, Instruccion[1]);
  not not_9 (nf2, Instruccion[2]);
  not not_10 (nf3, Instruccion[3]);
  not not_11 (nf4, Instruccion[4]);
  not not_12 (nf5, Instruccion[5]);
  assign {ConstanteExtendida[31:30], _4_offset[31:2]} = {{16{Instruccion[15]}}, Instruccion[15:0]};  // Bit_Extender bit_extender_1
  and and_1 (and_1_out, Instruccion[26], Instruccion[27], Instruccion[28], Instruccion[29], Instruccion[30], Instruccion[31]);
  and and_2 (and_2_out, np0, np1, np2, np3, np4, np5);
  not not_13 (not_13_out, and_3_out);
  and and_3 (and_3_out, nf0, nf1, nf2, Instruccion[3], nf4, nf5);
  and and_4 (and_4_out, Instruccion[26], Instruccion[27], Instruccion[28], Instruccion[29], Instruccion[30], Instruccion[31]);
  and and_5 (and_5_out, np0, np1, np2, np3, np4, np5);
  and and_6 (and_6_out, Instruccion[26], Instruccion[27], Instruccion[28], Instruccion[29], Instruccion[30], Instruccion[31]);
  and and_7 (and_7_out, np0, np1, np2, Instruccion[29], Instruccion[30], Instruccion[31]);
  not not_14 (not_14_out, and_1_out);
  and and_8 (and_8_out, and_2_out, not_13_out);
  or or_1 (or_1_out, and_5_out, and_6_out, and_7_out);
  assign or_2_out = 6'b110000 | Instruccion[5:0];  // OR_Gate or_2, 6 bits wide
  and and_9 (CodeSelector[0], not_14_out, not_15_out);
  not not_15 (not_15_out, and_8_out);
  not not_16 (not_16_out, or_1_out);
  assign or_3_out = 6'b111000 | Instruccion[5:0];  // OR_Gate or_3, 6 bits wide
  or or_4 (CodeSelector[2], and_4_out, not_16_out);
  Multiplexer #(.select(3), .width(6), .enable("false")) multiplexer_1 (
    .in0(6'b101001), .in1(6'b000011), .in2(Instruccion[5:0]), .in3(or_2_out), .in4(or_3_out),
    .in5(Instruccion[31:26]), .in6(6'b011111), .in7(6'b011111), .out(CODE), .sel(CodeSelector));
  // Probe on CodeSelector
  and and_10 (and_10_out, nf2, Instruccion[3], nf4);
  and and_11 (and_11_out, Instruccion[0], Instruccion[1], Instruccion[5]);
  or or_5 (or_5_out, and_11_out, and_12_out);
  and and_12 (and_12_out, nf0, nf1, nf5);
  // Probe on CODE
  and and_13 (and_13_out, np0, np1, np2, Instruccion[29], Instruccion[30], Instruccion[31]);
  and and_14 (and_14_out, np0, np1, np2, np3, np4, np5);
  not not_17 (not_17_out, and_15_out);
  and and_15 (and_15_out, and_10_out, or_5_out);
  and and_16 (and_16_out, and_14_out, not_17_out);
  or or_6 (CodeSelector[1], and_13_out, and_16_out);

  assign _4_offset[1:0] = 2'b00;
  assign Constante = Instruccion[15:0];
  assign ConstanteExtendida[29:0] = _4_offset[31:2];
  assign Destino_Salto = Instruccion[25:0];
  assign FUNCODE = Instruccion[5:0];
  assign OPCODE = Instruccion[31:26];
  assign Rd = Instruccion[15:11];
  assign Rs = Instruccion[25:21];
  assign Rt = Instruccion[20:16];

  // Other names for the same wires on the sheet: f0 = Instruccion[0]; f1 = Instruccion[1]; f2 = Instruccion[2];
  //   f3 = Instruccion[3]; f4 = Instruccion[4]; f5 = Instruccion[5]; p0 = Instruccion[26]; p1 = Instruccion[27];
  //   p2 = Instruccion[28]; p3 = Instruccion[29]; p4 = Instruccion[30]; p5 = Instruccion[31]

  // Notes on the sheet:
  //   TIPO R
  //   TIPO I
  //   TIPO J
  //   Invalid State
  //   jr
  //   Ver algortimo de codificacion de instrucciones en D-CodificacionInstrucciones.txt
  //   stlu
  //   Salidas Estado
  //   Salidas Control
endmodule
