// Logisim project C-MemoryManager.circ as structural Verilog: 1 circuit, main circuit MemoryManager
module MemoryManager (
  input  [31:0] Program_Counter_Address,
  input  [31:0] Ram_out_0,
  input  [31:0] Ram_out_1,
  input  [31:0] Ram_out_2,
  input  [31:0] Ram_out_3,
  input  [3:0] Read_Time,
  input  [3:0] Write_Time,
  input  CONTROL_SIGNALS,
  input  in_9,
  input  in_10,
  output [15:0] Address,
  output [31:0] Instruction,
  output Chip_Select,
  output Read_Write,
  output out_15
);

  wire d_ff_1_q, demultiplexer_1_out0, demultiplexer_1_out1, timer_1_end;
  wire [31:0] RAM_OUT_0_t, RAM_OUT_1_t, RAM_OUT_2_t, RAM_OUT_3_t;

  LittleToBigEndian littletobigendian_1 (.in_1(Ram_out_0), .out_2(RAM_OUT_0_t));
  LittleToBigEndian littletobigendian_2 (.in_1(Ram_out_1), .out_2(RAM_OUT_1_t));
  LittleToBigEndian littletobigendian_3 (.in_1(Ram_out_2), .out_2(RAM_OUT_2_t));
  LittleToBigEndian littletobigendian_4 (.in_1(Ram_out_3), .out_2(RAM_OUT_3_t));
  D_Flip_Flop d_ff_1 (
    .clk(CONTROL_SIGNALS), .D(demultiplexer_1_out0), .Q(d_ff_1_q), .preset(in_9));  // open: Qn, en, reset
  Demultiplexer #(.enable("false")) demultiplexer_1 (
    .out0(demultiplexer_1_out0), .out1(demultiplexer_1_out1), .in(d_ff_1_q), .sel(in_10));
  Timer timer_1 (
    .Start(demultiplexer_1_out1), .Reset(in_9), .Clock(CONTROL_SIGNALS), .Time(Read_Time), .END(timer_1_end));
  Multiplexer #(.select(2), .width(32), .enable("false")) multiplexer_1 (
    .in0(RAM_OUT_0_t), .in1(RAM_OUT_1_t), .in2(RAM_OUT_2_t), .in3(RAM_OUT_3_t), .out(Instruction),
    .sel(Program_Counter_Address[3:2]));

  assign Address = Program_Counter_Address[19:4];

  // Other names for the same wires on the sheet: CLK = CONTROL_SIGNALS; CS = Chip_Select; END = out_15;
  //   OFFSET[1:0] = Program_Counter_Address[3:2]; LINEA[15:0] = Program_Counter_Address[19:4]; RST = in_9;
  //   RW = Read_Write; START = in_10; WriteTime[3:0] = Write_Time

  // Notes on the sheet:
  //   RAM TIMING
  //   RAM CONTROL
  //   Los primeros
  //   20 bits de la direccion
  //   son los que interesan
  //   RAM ADDRESS
  //   DATA FROM RAM
  //   LINEA
  //   Los 16 bits mas significativos
  //   dan la linea que contiene la direccion
  //   Bytes direccionables = lineas * bytes por linea
  //   2^20 = 2^16 * 2^4
  //   linea de memoria = direccion / 16
  //   OFFSET
  //   LINEA
  //   Los 4 bits menos significativos
  //   dan el byte especifico en la linea
  //   al que apunta la direccion
  //   Los dos bits mas significativos
  //   representan el bloque de 4 bytes al que pertenece
  //   la direccion en la linea
endmodule
