// Logisim project C-RamReader.circ as structural Verilog: 1 circuit, main circuit RamReader
module RamReader (
  input  [31:0] ADDRESS_IN,
  input  [31:0] Ram_out_0,
  input  [31:0] Ram_out_1,
  input  [31:0] Ram_out_2,
  input  [31:0] Ram_out_3,
  input  [3:0] Read_Time,
  input  CLK,
  input  RST,
  input  START,
  output [15:0] Address,
  output [31:0] RAM_OUT,
  output [3:0] RAM_MASK,
  output Chip_Select,
  output Read_Write,
  output END
);

  wire CS0, d_ff_1_q, d_ff_2_q, demultiplexer_1_out0, demultiplexer_1_out1, MATCH, or_1_out, or_2_out;
  wire [3:0] counter_1_q;
  wire [31:0] RAM_OUT_0_t, RAM_OUT_1_t, RAM_OUT_2_t, RAM_OUT_3_t;

  LittleToBigEndian littletobigendian_1 (.in_1(Ram_out_0), .out_2(RAM_OUT_0_t));
  LittleToBigEndian littletobigendian_2 (.in_1(Ram_out_1), .out_2(RAM_OUT_1_t));
  LittleToBigEndian littletobigendian_3 (.in_1(Ram_out_2), .out_2(RAM_OUT_2_t));
  LittleToBigEndian littletobigendian_4 (.in_1(Ram_out_3), .out_2(RAM_OUT_3_t));
  or or_1 (or_1_out, demultiplexer_1_out0, END);
  D_Flip_Flop d_ff_1 (.clk(CLK), .D(or_1_out), .Q(d_ff_1_q), .preset(RST));  // open: Qn, en, reset
  Demultiplexer #(.enable("false")) demultiplexer_1 (
    .out0(demultiplexer_1_out0), .out1(demultiplexer_1_out1), .in(d_ff_1_q), .sel(START));
  or or_2 (or_2_out, CS0, demultiplexer_1_out1);
  D_Flip_Flop d_ff_2 (.clk(CLK), .D(or_2_out), .Q(d_ff_2_q), .reset(RST));  // open: Qn, preset, en
  Multiplexer #(.select(2), .width(32), .enable("false")) multiplexer_1 (
    .in0(RAM_OUT_0_t), .in1(RAM_OUT_1_t), .in2(RAM_OUT_2_t), .in3(RAM_OUT_3_t), .out(RAM_OUT),
    .sel(ADDRESS_IN[3:2]));
  Demultiplexer #(.enable("false")) demultiplexer_2 (.out0(CS0), .out1(END), .in(d_ff_2_q), .sel(MATCH));
  Counter #(.width(4), .max('hf)) counter_1 (.Q(counter_1_q), .clk(CLK), .clr(START));  // open: load, D, count, carry
  or or_3 (Chip_Select, CS0, END);
  Comparator #(.width(4)) comparator_1 (.a(Read_Time), .b(counter_1_q), .eq(MATCH));  // open: gt, lt

  assign Address = ADDRESS_IN[19:4];
  assign RAM_MASK = 4'b0000;
  assign Read_Write = 1'b0;

  // Other names for the same wires on the sheet: OFFSET[1:0] = ADDRESS_IN[3:2]; LINEA[15:0] = ADDRESS_IN[19:4];
  //   CS = Chip_Select; CS1 = END

  // Notes on the sheet:
  //   RAM TIMING
  //   RAM CONTROL
  //   Los primeros
  //   20 bits de la direccion
  //   son los que interesan
  //   RAM ADDRESS
  //   DATA FROM RAM
  //   LINEA
  //   Los 16 bits mas significativos
  //   dan la linea que contiene la direccion
  //   Bytes direccionables = lineas * bytes por linea
  //   2^20 = 2^16 * 2^4
  //   linea de memoria = direccion / 16
  //   CONTROL SIGNALS
  //   OFFSET
  //   LINEA
  //   Los 4 bits menos significativos
  //   dan el byte especifico en la linea
  //   al que apunta la direccion
  //   Los dos bits mas significativos
  //   representan el bloque de 4 bytes al que pertenece
  //   la direccion en la linea
  //   MINI DATA PATH
endmodule
