// Logisim project C-RamWritter.circ as structural Verilog: 1 circuit, main circuit RAM WRITTER
module RAM_WRITTER (
  input  [31:0] RAM_INPUT,
  input  [31:0] ADDRESS_IN,
  input  [3:0] Write_Time,
  input  CLK,
  input  RST,
  input  START,
  output [15:0] Address,
  output [31:0] RAM_IN_0,
  output [31:0] RAM_IN_1,
  output [31:0] RAM_IN_2,
  output [31:0] RAM_IN_3,
  output [3:0] RAM_MASK,
  output Chip_Select,
  output Read_Write,
  output END
);

  wire d_ff_1_q, d_ff_2_q, demultiplexer_1_out0, demultiplexer_1_out1, MATCH, or_1_out, or_2_out;
  wire [3:0] counter_1_q;

  BigToLittleEndian bigtolittleendian_1 (.in_1(RAM_INPUT), .out_2(RAM_IN_0));
  BigToLittleEndian bigtolittleendian_2 (.in_1(RAM_INPUT), .out_2(RAM_IN_1));
  BigToLittleEndian bigtolittleendian_3 (.in_1(RAM_INPUT), .out_2(RAM_IN_2));
  BigToLittleEndian bigtolittleendian_4 (.in_1(RAM_INPUT), .out_2(RAM_IN_3));
  or or_1 (or_1_out, demultiplexer_1_out0, END);
  D_Flip_Flop d_ff_1 (.clk(CLK), .D(or_1_out), .Q(d_ff_1_q), .preset(RST));  // open: Qn, en, reset
  Demultiplexer #(.enable("false")) demultiplexer_1 (
    .out0(demultiplexer_1_out0), .out1(demultiplexer_1_out1), .in(d_ff_1_q), .sel(START));
  or or_2 (or_2_out, Read_Write, demultiplexer_1_out1);
  Counter #(.width(4), .max('hf)) counter_1 (.Q(counter_1_q), .clk(CLK), .clr(START));  // open: load, D, count, carry
  or or_3 (Chip_Select, Read_Write, END);
  Demultiplexer #(.enable("false")) demultiplexer_2 (.out0(Read_Write), .out1(END), .in(d_ff_2_q), .sel(MATCH));
  D_Flip_Flop d_ff_2 (.clk(CLK), .D(or_2_out), .Q(d_ff_2_q), .reset(RST));  // open: Qn, preset, en
  Comparator #(.width(4)) comparator_1 (.a(Write_Time), .b(counter_1_q), .eq(MATCH));  // open: gt, lt
  Demultiplexer #(.select(2), .enable("false")) demultiplexer_3 (
    .out0(RAM_MASK[0]), .out1(RAM_MASK[1]), .out2(RAM_MASK[2]), .out3(RAM_MASK[3]), .in(Read_Write),
    .sel(ADDRESS_IN[3:2]));

  assign Address = ADDRESS_IN[19:4];

  // Other names for the same wires on the sheet: OFFSET[1:0] = ADDRESS_IN[3:2]; LINEA[15:0] = ADDRESS_IN[19:4];
  //   CS = Chip_Select; CS1 = END; MASK[3:0] = RAM_MASK; RAM_IN[31:0] = RAM_INPUT; CS0 = Read_Write;
  //   MASK_IN = Read_Write; WRITE = Read_Write

  // Notes on the sheet:
  //   RAM TIMING
  //   RAM CONTROL
  //   Los primeros
  //   20 bits de la direccion
  //   son los que interesan
  //   RAM ADDRESS
  //   DATA TO RAM
  //   LINEA
  //   Los 16 bits mas significativos
  //   dan la linea que contiene la direccion
  //   Bytes direccionables = lineas * bytes por linea
  //   2^20 = 2^16 * 2^4
  //   linea de memoria = direccion / 16
  //   CONTROL SIGNALS
  //   OFFSET
  //   LINEA
  //   Los 4 bits menos significativos
  //   dan el byte especifico en la linea
  //   al que apunta la direccion
  //   Los dos bits mas significativos
  //   representan el bloque de 4 bytes al que pertenece
  //   la direccion en la linea
  //   MINI DATA PATH
endmodule
