// Logisim project C-RegisterFile.circ as structural Verilog: 1 circuit, main circuit RegisterFile
module RegisterFile (
  input  CLK,
  input  [4:0] DESTINATION_ADDRESS,
  input  RST,
  input  READ_WRITE,
  input  [31:0] DATA_INPUT,
  input  [31:0] LO_IN,
  input  Load_LO,
  input  [31:0] HI_IN,
  input  Load_HI,
  input  [4:0] SELECTOR_A,
  input  [4:0] SELECTOR_B,
  output [31:0] LO_OUT,
  output [31:0] OUTPUT_REGISTER_A,
  output [31:0] OUTPUT_REGISTER_B,
  output [31:0] SP,
  output [31:0] HI_OUT
);

  wire L1, L2, L3, L4, L5, L6, L7, L8, L9, L10, L11, L12, L13, L14, L15, L16, L17, L18, L19, L20, L21, L22,
       L23, L24, L25, L26, L27, L28, L29, L30, L31;
  wire [31:0] R0, R1, R2, R3, R4, R5, R6, R7, R8, R9, R10, R11, R12, R13, R14, R15, R16, R17, R18, R19, R20,
       R21, R22, R23, R24, R25, R26, R27, R28, R29, R30;

  Demultiplexer #(.select(5), .enable("false")) demultiplexer_1 (
    .out1(L1), .out2(L2), .out3(L3), .out4(L4), .out5(L5), .out6(L6), .out7(L7), .out8(L8), .out9(L9),
    .out10(L10), .out11(L11), .out12(L12), .out13(L13), .out14(L14), .out15(L15), .out16(L16), .out17(L17),
    .out18(L18), .out19(L19), .out20(L20), .out21(L21), .out22(L22), .out23(L23), .out24(L24), .out25(L25),
    .out26(L26), .out27(L27), .out28(L28), .out29(L29), .out30(L30), .out31(L31), .in(READ_WRITE),
    .sel(DESTINATION_ADDRESS));  // open: out0
  Register #(.width(32)) u_R0 (.Q(R0), .clk(CLK), .clr(RST));  // open: D, en
  Register #(.width(32)) u_R1 (.D(DATA_INPUT), .en(L1), .Q(R1), .clk(CLK), .clr(RST));
  Register #(.width(32)) u_R5 (.D(DATA_INPUT), .en(L5), .Q(R5), .clk(CLK), .clr(RST));
  Register #(.width(32)) u_R9 (.D(DATA_INPUT), .en(L9), .Q(R9), .clk(CLK), .clr(RST));
  Register #(.width(32)) u_R13 (.D(DATA_INPUT), .en(L13), .Q(R13), .clk(CLK), .clr(RST));
  Register #(.width(32)) u_R2 (.D(DATA_INPUT), .en(L2), .Q(R2), .clk(CLK), .clr(RST));
  Register #(.width(32)) u_R6 (.D(DATA_INPUT), .en(L6), .Q(R6), .clk(CLK), .clr(RST));
  Register #(.width(32)) u_R10 (.D(DATA_INPUT), .en(L10), .Q(R10), .clk(CLK), .clr(RST));
  Register #(.width(32)) u_R14 (.D(DATA_INPUT), .en(L14), .Q(R14), .clk(CLK), .clr(RST));
  Register #(.width(32)) u_R3 (.D(DATA_INPUT), .en(L3), .Q(R3), .clk(CLK), .clr(RST));
  Register #(.width(32)) u_R7 (.D(DATA_INPUT), .en(L7), .Q(R7), .clk(CLK), .clr(RST));
  Register #(.width(32)) u_R11 (.D(DATA_INPUT), .en(L11), .Q(R11), .clk(CLK), .clr(RST));
  Register #(.width(32)) u_R15 (.D(DATA_INPUT), .en(L15), .Q(R15), .clk(CLK), .clr(RST));
  Multiplexer #(.select(5), .width(32), .enable("false")) multiplexer_1 (
    .in0(R0), .in1(R1), .in2(R2), .in3(R3), .in4(R4), .in5(R5), .in6(R6), .in7(R7), .in8(R8), .in9(R9),
    .in10(R10), .in11(R11), .in12(R12), .in13(R13), .in14(R14), .in15(R15), .in16(R16), .in17(R17),
    .in18(R18), .in19(R19), .in20(R20), .in21(R21), .in22(R22), .in23(R23), .in24(R24), .in25(R25),
    .in26(R26), .in27(R27), .in28(R28), .in29(R29), .in30(R30), .in31(SP), .out(OUTPUT_REGISTER_A),
    .sel(SELECTOR_A));
  Register #(.width(32)) u_R4 (.D(DATA_INPUT), .en(L4), .Q(R4), .clk(CLK), .clr(RST));
  Register #(.width(32)) u_R8 (.D(DATA_INPUT), .en(L8), .Q(R8), .clk(CLK), .clr(RST));
  Register #(.width(32)) u_R12 (.D(DATA_INPUT), .en(L12), .Q(R12), .clk(CLK), .clr(RST));
  Register #(.width(32)) u_R16 (.D(DATA_INPUT), .en(L16), .Q(R16), .clk(CLK), .clr(RST));
  Register #(.width(32)) u_R17 (.D(DATA_INPUT), .en(L17), .Q(R17), .clk(CLK), .clr(RST));
  Register #(.width(32)) u_R21 (.D(DATA_INPUT), .en(L21), .Q(R21), .clk(CLK), .clr(RST));
  Register #(.width(32)) u_R25 (.D(DATA_INPUT), .en(L25), .Q(R25), .clk(CLK), .clr(RST));
  Register #(.width(32)) u_R29 (.D(DATA_INPUT), .en(L29), .Q(R29), .clk(CLK), .clr(RST));
  Multiplexer #(.select(5), .width(32), .enable("false")) multiplexer_2 (
    .in0(R0), .in1(R1), .in2(R2), .in3(R3), .in4(R4), .in5(R5), .in6(R6), .in7(R7), .in8(R8), .in9(R9),
    .in10(R10), .in11(R11), .in12(R12), .in13(R13), .in14(R14), .in15(R15), .in16(R16), .in17(R17),
    .in18(R18), .in19(R19), .in20(R20), .in21(R21), .in22(R22), .in23(R23), .in24(R24), .in25(R25),
    .in26(R26), .in27(R27), .in28(R28), .in29(R29), .in30(R30), .in31(SP), .out(OUTPUT_REGISTER_B),
    .sel(SELECTOR_B));
  Register #(.width(32)) u_R18 (.D(DATA_INPUT), .en(L18), .Q(R18), .clk(CLK), .clr(RST));
  Register #(.width(32)) u_R22 (.D(DATA_INPUT), .en(L22), .Q(R22), .clk(CLK), .clr(RST));
  Register #(.width(32)) u_R26 (.D(DATA_INPUT), .en(L26), .Q(R26), .clk(CLK), .clr(RST));
  Register #(.width(32)) u_R30 (.D(DATA_INPUT), .en(L30), .Q(R30), .clk(CLK), .clr(RST));
  Register #(.width(32)) u_R19 (.D(DATA_INPUT), .en(L19), .Q(R19), .clk(CLK), .clr(RST));
  Register #(.width(32)) u_R23 (.D(DATA_INPUT), .en(L23), .Q(R23), .clk(CLK), .clr(RST));
  Register #(.width(32)) u_R27 (.D(DATA_INPUT), .en(L27), .Q(R27), .clk(CLK), .clr(RST));
  Register #(.width(32)) R31 (.D(DATA_INPUT), .en(L31), .Q(SP), .clk(CLK), .clr(RST));
  Register #(.width(32)) LO (.D(LO_IN), .en(Load_LO), .Q(LO_OUT), .clk(CLK), .clr(RST));
  Register #(.width(32)) HI (.D(HI_IN), .en(Load_HI), .Q(HI_OUT), .clk(CLK), .clr(RST));
  Register #(.width(32)) u_R20 (.D(DATA_INPUT), .en(L20), .Q(R20), .clk(CLK), .clr(RST));
  Register #(.width(32)) u_R24 (.D(DATA_INPUT), .en(L24), .Q(R24), .clk(CLK), .clr(RST));
  Register #(.width(32)) u_R28 (.D(DATA_INPUT), .en(L28), .Q(R28), .clk(CLK), .clr(RST));

  // Other names for the same wires on the sheet: DATA_IN[31:0] = DATA_INPUT; R31[31:0] = SP; R_W = READ_WRITE;
  //   SA[4:0] = SELECTOR_A; SB[4:0] = SELECTOR_B; WRITE_ADRRESS[4:0] = DESTINATION_ADDRESS

  // Notes on the sheet:
  //   REGISTERS 1 TO 16
  //   REGISTERS 17 TO 31
  //   SP
  //   HI and LO
endmodule
