// Logisim project C-Timer.circ as structural Verilog: 1 circuit, main circuit Timer
module Timer (
  input  Start,
  input  Reset,
  input  Clock,
  input  [3:0] Time,
  output END
);

  wire [3:0] counter_1_q;

  Counter #(.width(4), .max('hf)) counter_1 (
    .count(Start), .Q(counter_1_q), .clk(Clock), .clr(Reset));  // open: load, D, carry
  Comparator #(.width(4)) comparator_1 (.a(Time), .b(counter_1_q), .eq(END));  // open: gt, lt

  // Other names for the same wires on the sheet: CLK = Clock; RST = Reset
endmodule
