// Logisim project s-mips.circ as structural Verilog: 4 circuits, main circuit S-MIPS Board
module S_MIPS_Board (
  input  DESHABILITAR_DISPATCHER,
  output halt
);

  wire button_1_out, CLK, CS, d_ff_1_q, LCLR, LoadRAM, LoadRAMOn, LW, R_R_W, R_W, ram_dispatcher_1_finished,
       RCS, Reset_out, RST, TTY_EN;
  wire [2:0] KDB;
  wire [3:0] LMask, Mask, ram_1_read_time, ram_1_write_time, RMask;
  wire [6:0] KDB_DATA, TTY_DATA;
  wire [15:0] Addr, LAddr, RAddr;
  wire [31:0] I0, I1, I2, I3, LData, ram_1_data_out_0, ram_1_data_out_1, ram_1_data_out_2, ram_1_data_out_3,
       RI0, RI1, RI2, RI3;

  TTY #(.rows(25), .cols(80)) tty_1 (.data(TTY_DATA), .clk(CLK), .we(TTY_EN), .clr(RST));
  not not_1 (LoadRAMOn, ram_dispatcher_1_finished);
  RAM_Dispatcher ram_dispatcher_1 (
    .WriteTime(ram_1_write_time), .Clock(CLK), .Data(LData), .Address(LAddr), .Mask(LMask),
    .Finished(ram_dispatcher_1_finished), .Write(LW), .CLR(LCLR));
  Keyboard #(.buflen(64)) keyboard_1 (.clk(CLK), .re(KDB[0]), .avail(KDB[2]), .data(KDB_DATA));  // open: clr
  RAM ram_1 (
    .Address(RAddr), .Data_Out_0(ram_1_data_out_0), .Data_Out_1(ram_1_data_out_1),
    .Data_Out_2(ram_1_data_out_2), .Data_Out_3(ram_1_data_out_3), .Data_In_0(RI0), .Data_In_1(RI1),
    .Data_In_2(RI2), .Data_In_3(RI3), .Mask(RMask), .nRead_Write(R_R_W), .Chip_Select(RCS),
    .Read_Time(ram_1_read_time), .Reset(button_1_out), .Write_Time(ram_1_write_time));
  Button button_1 (.out(button_1_out));
  D_Flip_Flop d_ff_1 (.clk(CLK), .D(1'b1), .Q(d_ff_1_q), .reset(Reset_out));  // open: Qn, preset, en
  Button Reset (.out(Reset_out));
  S_MIPS s_mips_1 (
    .Kbd_Enable(KDB[0]), .Address(Addr), .Kbd_Clear(KDB[1]), .Kbd_Available(KDB[2]), .RAM_In_0(I0),
    .Kbd_ASCII_Data(KDB_DATA), .RAM_In_1(I1), .TTY_Enable(TTY_EN), .RAM_In_2(I2), .RAM_In_3(I3),
    .TTY_ASCII_Data(TTY_DATA), .Reset(RST), .RAM_Out_0(ram_1_data_out_0), .Clock(CLK),
    .RAM_Out_1(ram_1_data_out_1), .Stop(halt), .RAM_Out_2(ram_1_data_out_2), .RAM_Out_3(ram_1_data_out_3),
    .Mask(Mask), .Read_Time(ram_1_read_time), .Write_Time(ram_1_write_time), .nRead_Write(R_W),
    .Chip_Select(CS));
  D_Flip_Flop d_ff_2 (.clk(CLK), .D(d_ff_1_q), .Qn(LCLR), .reset(Reset_out));  // open: Q, preset, en
  or or_1 (RST, LCLR, LoadRAM);
  Clock clock_1 (.out(CLK));
  Multiplexer #(.width(32), .enable("false")) multiplexer_1 (.in0(I0), .in1(LData), .out(RI0), .sel(LoadRAM));
  Multiplexer #(.width(32), .enable("false")) multiplexer_2 (.in0(I1), .in1(LData), .out(RI1), .sel(LoadRAM));
  Multiplexer #(.width(32), .enable("false")) multiplexer_3 (.in0(I2), .in1(LData), .out(RI2), .sel(LoadRAM));
  Multiplexer #(.width(32), .enable("false")) multiplexer_4 (.in0(I3), .in1(LData), .out(RI3), .sel(LoadRAM));
  and and_1 (LoadRAM, ~DESHABILITAR_DISPATCHER, LoadRAMOn);  // AND_Gate
  Multiplexer #(.width(16), .enable("false")) multiplexer_5 (.in0(Addr), .in1(LAddr), .out(RAddr), .sel(LoadRAM));
  Multiplexer #(.width(4), .enable("false")) multiplexer_6 (.in0(Mask), .in1(LMask), .out(RMask), .sel(LoadRAM));
  Multiplexer #(.enable("false")) multiplexer_7 (.in0(CS), .in1(LW), .out(RCS), .sel(LoadRAM));
  Multiplexer #(.enable("false")) multiplexer_8 (.in0(R_W), .in1(LW), .out(R_R_W), .sel(LoadRAM));

  // Notes on the sheet:
  //   NO MODIFICAR
  //   Keyboard
endmodule

module RAM (
  input  [15:0] Address,
  input  [31:0] Data_In_0,
  input  [31:0] Data_In_1,
  input  [31:0] Data_In_2,
  input  [31:0] Data_In_3,
  input  [3:0] Mask,
  input  nRead_Write,
  input  Chip_Select,
  input  Reset,
  output [31:0] Data_Out_0,
  output [31:0] Data_Out_1,
  output [31:0] Data_Out_2,
  output [31:0] Data_Out_3,
  output [3:0] Read_Time,
  output [3:0] Write_Time
);

  wire and_2_out, and_3_out, and_4_out, and_5_out, and_6_out, and_7_out, and_8_out, and_9_out, Changed, CLK,
       comparator_2_eq, comparator_3_eq, comparator_4_eq, comparator_5_eq, comparator_6_eq, Count,
       demultiplexer_3_out0, Idle, Idle_q, Load, Load0, Load1, nand_1_out, or_1_out, or_2_out, or_3_out,
       or_4_out, or_5_out, or_6_out, or_7_out, or_8_out, or_9_out, or_10_out, Proc_q, Update_Mem, Zero_Time;
  wire [3:0] counter_1_q, multiplexer_1_out, subtractor_1_out;
  wire [31:0] register_1_q, register_2_q, register_3_q, register_4_q, register_5_q;

  // Probe on 4'b0011
  // Probe on 4'b0010
  Multiplexer #(.width(4), .enable("false")) multiplexer_1 (
    .in0(4'b0011), .in1(4'b0010), .out(multiplexer_1_out), .sel(nRead_Write));
  or or_1 (or_1_out, Idle, Update_Mem);
  or or_2 (or_2_out, ~Chip_Select, Reset);  // OR_Gate
  Subtractor #(.width(4)) subtractor_1 (.a(multiplexer_1_out), .b(4'b0010), .out(subtractor_1_out));  // open: bin, bout
  Demultiplexer #(.enable("false")) demultiplexer_1 (.out0(Idle), .out1(Load0), .in(Idle_q), .sel(Changed));
  D_Flip_Flop u_Idle (.clk(CLK), .D(or_1_out), .Q(Idle_q), .preset(or_2_out));  // open: Qn, en, reset
  // Probe on counter_1_q
  Counter #(.width(4), .max('hf)) counter_1 (
    .load(Load), .D(subtractor_1_out), .count(Count), .Q(counter_1_q), .clk(CLK), .clr(or_3_out));  // open: carry
  or or_3 (or_3_out, ~Chip_Select, Reset);  // OR_Gate
  Comparator #(.width(4), .mode("unsigned")) comparator_1 (
    .a(4'b0000), .b(counter_1_q), .eq(Zero_Time));  // open: gt, lt
  or or_4 (or_4_out, Count, Load0, Load1);
  Register #(.width(32)) register_1 (.D(Data_In_0), .en(Chip_Select), .Q(register_1_q), .clk(CLK), .clr(or_5_out));
  or or_5 (or_5_out, ~Chip_Select, Reset);  // OR_Gate
  Register #(.width(32)) register_2 (.D(Data_In_1), .en(Chip_Select), .Q(register_2_q), .clk(CLK), .clr(or_6_out));
  or or_6 (or_6_out, ~Chip_Select, Reset);  // OR_Gate
  Register #(.width(32)) register_3 (.D(Data_In_2), .en(Chip_Select), .Q(register_3_q), .clk(CLK), .clr(or_7_out));
  or or_7 (or_7_out, ~Chip_Select, Reset);  // OR_Gate
  Register #(.width(32)) register_4 (.D(Data_In_3), .en(Chip_Select), .Q(register_4_q), .clk(CLK), .clr(or_8_out));
  or or_8 (or_8_out, ~Chip_Select, Reset);  // OR_Gate
  Register #(.width(32)) register_5 (
    .D({{11{1'b1}}, nRead_Write, Mask, Address}), .en(Chip_Select), .Q(register_5_q), .clk(CLK),
    .clr(or_9_out));
  or or_9 (or_9_out, ~Chip_Select, Reset);  // OR_Gate
  D_Flip_Flop Proc (.clk(CLK), .D(or_4_out), .Q(Proc_q), .reset(or_10_out));  // open: Qn, preset, en
  or or_10 (or_10_out, ~Chip_Select, Reset);  // OR_Gate
  Demultiplexer #(.enable("false")) demultiplexer_2 (
    .out0(Count), .out1(Update_Mem), .in(demultiplexer_3_out0), .sel(Zero_Time));
  Demultiplexer #(.enable("false")) demultiplexer_3 (
    .out0(demultiplexer_3_out0), .out1(Load1), .in(Proc_q), .sel(Changed));
  Clock clock_1 (.out(CLK));
  Comparator #(.width(32)) comparator_2 (.a(register_1_q), .b(Data_In_0), .eq(comparator_2_eq));  // open: gt, lt
  Comparator #(.width(32)) comparator_3 (.a(register_2_q), .b(Data_In_1), .eq(comparator_3_eq));  // open: gt, lt
  Comparator #(.width(32)) comparator_4 (.a(register_3_q), .b(Data_In_2), .eq(comparator_4_eq));  // open: gt, lt
  Comparator #(.width(32)) comparator_5 (.a(register_4_q), .b(Data_In_3), .eq(comparator_5_eq));  // open: gt, lt
  Comparator #(.width(32)) comparator_6 (
    .a(register_5_q), .b({{11{1'b1}}, nRead_Write, Mask, Address}), .eq(comparator_6_eq));  // open: gt, lt
  nand nand_1 (nand_1_out, comparator_6_eq, comparator_2_eq, comparator_3_eq, comparator_4_eq, comparator_5_eq);
  and and_1 (Changed, nand_1_out, Chip_Select);
  or or_11 (Load, Count, Load1, Load0);
  and and_2 (and_2_out, Mask[0], Update_Mem, nRead_Write);
  and and_3 (and_3_out, Mask[1], Update_Mem, nRead_Write);
  and and_4 (and_4_out, Mask[2], Update_Mem, nRead_Write);
  and and_5 (and_5_out, Mask[3], Update_Mem, nRead_Write);
  RAM_part #(.addrWidth(16), .dataWidth(32), .bus("separate")) ram_1 (
    .addr(Address), .din(Data_In_0), .data(Data_Out_0), .str(and_2_out), .sel(Chip_Select), .clk(CLK),
    .ld(and_6_out), .clr(Reset));
  and and_6 (and_6_out, ~nRead_Write, Idle);  // AND_Gate
  RAM_part #(.addrWidth(16), .dataWidth(32), .bus("separate")) ram_2 (
    .addr(Address), .din(Data_In_1), .data(Data_Out_1), .str(and_3_out), .sel(Chip_Select), .clk(CLK),
    .ld(and_7_out), .clr(Reset));
  and and_7 (and_7_out, ~nRead_Write, Idle);  // AND_Gate
  RAM_part #(.addrWidth(16), .dataWidth(32), .bus("separate")) ram_3 (
    .addr(Address), .din(Data_In_2), .data(Data_Out_2), .str(and_4_out), .sel(Chip_Select), .clk(CLK),
    .ld(and_8_out), .clr(Reset));
  and and_8 (and_8_out, ~nRead_Write, Idle);  // AND_Gate
  RAM_part #(.addrWidth(16), .dataWidth(32), .bus("separate")) ram_4 (
    .addr(Address), .din(Data_In_3), .data(Data_Out_3), .str(and_5_out), .sel(Chip_Select), .clk(CLK),
    .ld(and_9_out), .clr(Reset));
  and and_9 (and_9_out, ~nRead_Write, Idle);  // AND_Gate

  assign Read_Time = 4'b0011;
  assign Write_Time = 4'b0010;

  // Other names for the same wires on the sheet: M0 = Mask[0]; M1 = Mask[1]; M2 = Mask[2]; M3 = Mask[3];
  //   RW = nRead_Write; CLR = Reset; CS = Chip_Select; Load2 = Count

  // Notes on the sheet:
  //   NO MODIFICAR
  //   excepto quizás los valores RT y WT
  //   BANK0
  //   BANK1
  //   BANK2
  //   BANK3
endmodule

module S_MIPS (
  input  Kbd_Available,
  input  [6:0] Kbd_ASCII_Data,
  input  [31:0] RAM_Out_0,
  input  [31:0] RAM_Out_1,
  input  Reset,
  input  [31:0] RAM_Out_2,
  input  Clock,
  input  [31:0] RAM_Out_3,
  input  [3:0] Read_Time,
  input  [3:0] Write_Time,
  output Kbd_Enable,
  output [15:0] Address,
  output Kbd_Clear,
  output TTY_Enable,
  output [6:0] TTY_ASCII_Data,
  output Stop,
  output [31:0] RAM_In_0,
  output [31:0] RAM_In_1,
  output [31:0] RAM_In_2,
  output [31:0] RAM_In_3,
  output [3:0] Mask,
  output nRead_Write,
  output Chip_Select
);

  wire END_READ, END_WRITE, FETCH_INSTRUCTION, LOAD_HI, LOAD_LO, LoadIR, LoadPC, MEMORY_OP_SELECTOR, NF,
       READER_CS, READER_R_W, STACK_OPERATION, START_READ, START_WRITE, WRITE_RF, WRITTER_CS, WRITTER_R_W, ZF;
  wire [1:0] AddressSelector, ALU_SELECTOR_A, BRANCH_SELECTOR;
  wire [2:0] ALU_SELECTOR_B, DataSelector;
  wire [3:0] ALU_Op, READER_MASK, WRITER_MASK;
  wire [4:0] multiplexer_3_out, RD, RS, RT;
  wire [5:0] CODE;
  wire [15:0] READER_ADDRESS, WRITTER_ADDRESS;
  wire [27:0] PC;
  wire [31:0] _4_offset, ALU_HI, ALU_LO, ALU_RESULT, \const , HI, IR, LO, multiplexer_1_out,
       multiplexer_2_out, multiplexer_4_out, multiplexer_5_out, multiplexer_6_out, multiplexer_9_out,
       multiplexer_11_out, NextInstruction, RAM_OUT, RANDOM_NUMBER, RB, SP;
  wire [31:2] DESTINO;
  wire [31:7] RA;

  Multiplexer #(.select(2), .width(32), .enable("false")) multiplexer_1 (
    .in0({DESTINO[31:28], PC}), .in1({RA, TTY_ASCII_Data}), .in2(SP), .out(multiplexer_1_out),
    .sel(ALU_SELECTOR_A));  // open: in3
  Multiplexer #(.select(3), .width(32), .enable("false")) multiplexer_2 (
    .in0(32'h4), .in1(RB), .in2(\const ), .in3({32{1'b0}}), .in4(_4_offset), .out(multiplexer_2_out),
    .sel(ALU_SELECTOR_B));  // open: in5, in6, in7
  ALU alu_1 (
    .in_1(multiplexer_1_out), .in_2(multiplexer_2_out), .in_3(ALU_Op), .out_4(ALU_RESULT), .out_5(ALU_LO),
    .out_6(ALU_HI), .ZeroFlag(ZF), .NegativeFlag(NF));
  Multiplexer #(.select(2), .width(5), .enable("false")) multiplexer_3 (
    .in0(RD), .in1(RT), .in2({5{1'b1}}), .out(multiplexer_3_out), .sel(AddressSelector));  // open: in3
  RegisterFile registerfile_1 (
    .CLK(Clock), .DESTINATION_ADDRESS(multiplexer_3_out), .RST(Reset), .READ_WRITE(WRITE_RF),
    .DATA_INPUT(multiplexer_4_out), .OUTPUT_REGISTER_A({RA, TTY_ASCII_Data}), .OUTPUT_REGISTER_B(RB),
    .SELECTOR_A(RS), .SELECTOR_B(RT), .HI_IN(ALU_HI), .Load_HI(LOAD_HI), .LO_IN(ALU_LO), .Load_LO(LOAD_LO),
    .HI_OUT(HI), .LO_OUT(LO), .SP(SP));
  Multiplexer #(.select(3), .width(32), .enable("false")) multiplexer_4 (
    .in0(ALU_RESULT), .in1(LO), .in2(HI), .in3(RANDOM_NUMBER), .in4(RAM_OUT), .out(multiplexer_4_out),
    .sel(DataSelector));  // open: in5, in6, in7
  Multiplexer #(.select(2), .width(32), .enable("false")) multiplexer_5 (
    .in0(ALU_RESULT), .in1({DESTINO, 2'b00}), .in2({RA, TTY_ASCII_Data}), .in3(RAM_OUT),
    .out(multiplexer_5_out), .sel(BRANCH_SELECTOR));
  BranchControl branchcontrol_1 (.Instruction_Address(multiplexer_5_out), .Next_Instruction_Address(NextInstruction));
  ControlUnit controlunit_1 (
    .LoadInstructionRegister(LoadIR), .CODE(CODE), .ALU_OP_SELECTOR(ALU_Op), .Load_PC(LoadPC), .STOP(Stop),
    .TTY_ENABLE(TTY_Enable), .ALU_SELECTOR_A(ALU_SELECTOR_A), .ALU_SELECTOR_B(ALU_SELECTOR_B),
    .WRITE_RF(WRITE_RF), .ADDRESS_SELECTOR(AddressSelector), .DATA_SELECTOR(DataSelector), .LOAD_HI(LOAD_HI),
    .LOAD_LO(LOAD_LO), .ZERO_FLAG(ZF), .NEGATIVE_FLAG(NF), .CLK(Clock), .RST(Reset),
    .BRANCH_SELECTOR(BRANCH_SELECTOR), .MEMORY_OP_SELECTOR(MEMORY_OP_SELECTOR), .START_READ(START_READ),
    .START_WRITE(START_WRITE), .END_READ(END_READ), .END_WRITE(END_WRITE),
    .FETCH_INSTRUCTION(FETCH_INSTRUCTION), .STACK_OPERATION(STACK_OPERATION));
  Register #(.width(32)) Program_Counter (
    .D(NextInstruction), .en(LoadPC), .Q({DESTINO[31:28], PC}), .clk(Clock), .clr(Reset));
  Random #(.width(32)) random_1 (.clk(Clock), .next(1'b1), .out(RANDOM_NUMBER));  // open: clr
  Multiplexer #(.select(2), .width(32), .enable("false")) multiplexer_6 (
    .in0(ALU_RESULT), .in1({DESTINO[31:28], PC}), .in2(SP), .out(multiplexer_6_out),
    .sel({STACK_OPERATION, FETCH_INSTRUCTION}));  // open: in3
  Register #(.width(32)) Instruction_Register (.D(NextInstruction), .en(LoadIR), .Q(IR), .clk(Clock), .clr(Reset));
  RamReader ramreader_1 (
    .ADDRESS_IN(multiplexer_6_out), .Address(READER_ADDRESS), .Ram_out_0(RAM_Out_0), .Ram_out_1(RAM_Out_1),
    .Ram_out_2(RAM_Out_2), .Ram_out_3(RAM_Out_3), .Read_Time(Read_Time), .RAM_MASK(READER_MASK), .CLK(Clock),
    .RST(Reset), .Chip_Select(READER_CS), .START(START_READ), .Read_Write(READER_R_W), .RAM_OUT(RAM_OUT),
    .END(END_READ));
  Multiplexer #(.width(4), .enable("false")) multiplexer_7 (
    .in0(READER_MASK), .in1(WRITER_MASK), .out(Mask), .sel(MEMORY_OP_SELECTOR));
  Multiplexer #(.enable("false")) multiplexer_8 (
    .in0(READER_R_W), .in1(WRITTER_R_W), .out(nRead_Write), .sel(MEMORY_OP_SELECTOR));
  Multiplexer #(.width(32), .enable("false")) multiplexer_9 (
    .in0(ALU_RESULT), .in1(SP), .out(multiplexer_9_out), .sel(STACK_OPERATION));
  Multiplexer #(.enable("false")) multiplexer_10 (
    .in0(READER_CS), .in1(WRITTER_CS), .out(Chip_Select), .sel(MEMORY_OP_SELECTOR));
  Multiplexer #(.width(32), .enable("false")) multiplexer_11 (
    .in0(RB), .in1({RA, TTY_ASCII_Data}), .out(multiplexer_11_out), .sel(STACK_OPERATION));
  RAM_WRITTER ram_writter_1 (
    .RAM_INPUT(multiplexer_11_out), .ADDRESS_IN(multiplexer_9_out), .Address(WRITTER_ADDRESS),
    .RAM_IN_0(RAM_In_0), .RAM_IN_1(RAM_In_1), .RAM_IN_2(RAM_In_2), .RAM_IN_3(RAM_In_3),
    .Write_Time(Write_Time), .RAM_MASK(WRITER_MASK), .CLK(Clock), .RST(Reset), .Chip_Select(WRITTER_CS),
    .START(START_WRITE), .Read_Write(WRITTER_R_W), .END(END_WRITE));
  Multiplexer #(.width(16), .enable("false")) multiplexer_12 (
    .in0(READER_ADDRESS), .in1(WRITTER_ADDRESS), .out(Address), .sel(MEMORY_OP_SELECTOR));
  InstructionDecoder instructiondecoder_1 (
    .Instruccion(IR), .Rs(RS), .Rt(RT), .Rd(RD), .Destino_Salto(DESTINO[27:2]), .CODE(CODE),
    .ConstanteExtendida(\const ), ._4_offset(_4_offset));  // open: OPCODE, FUNCODE, Constante

  assign Kbd_Clear = 1'b0;
  assign Kbd_Enable = 1'b0;
  // also tied to GND on the sheet: {Kbd_ASCII_Data[0], Kbd_ASCII_Data[1], Kbd_ASCII_Data[2], Kbd_ASCII_Data[3], Kbd_ASCII_Data[4], Kbd_ASCII_Data[5], Kbd_ASCII_Data[6]}

  // Other names for the same wires on the sheet: CLK = Clock; CS = Chip_Select; DESTINO_SALTO[25:0] = DESTINO[27:2];
  //   PC[31:28] = DESTINO[31:28]; KBD_AVAIL = Kbd_Available; KBD_DATA[6:0] = Kbd_ASCII_Data; RA[6:0] = TTY_ASCII_Data;
  //   TTY_DATA[6:0] = TTY_ASCII_Data; RAM_A[15:0] = Address; RAM_INPUT_0[31:0] = RAM_In_0;
  //   RAM_INPUT_1[31:0] = RAM_In_1; RAM_INPUT_2[31:0] = RAM_In_2; RAM_INPUT_3[31:0] = RAM_In_3; RAM_MASK[3:0] = Mask;
  //   RAM_OUTPUT_0[31:0] = RAM_Out_0; RAM_OUTPUT_1[31:0] = RAM_Out_1; RAM_OUTPUT_2[31:0] = RAM_Out_2;
  //   RAM_OUTPUT_3[31:0] = RAM_Out_3; RST = Reset; RW = nRead_Write

  // Notes on the sheet:
  //   RAM ADDRESS
  //   DATA FROM RAM
  //   DATA TO RAM
  //   DATA WRITE MASK
  //   RAM TIMING
  //   RAM CONTROL
  //   KEYBOARD
  //   TTY
  //   SEQUENCING
  //   ALU
  //   SP
  //   REGISTER FILE
  //   BRANCH CONTROL
  //   DATA PATH
  //   CONTROL UNIT
  //   CONTROL REGISTERS
  //   AUXILIARES
  //   INSTRUCTION DECODER
endmodule

module RAM_Dispatcher (
  input  [3:0] WriteTime,
  input  Clock,
  input  CLR,
  output [31:0] Data,
  output [15:0] Address,
  output [3:0] Mask,
  output Finished,
  output Write
);

  wire demultiplexer_2_out1, demultiplexer_3_out1, End, IDLE_q, IncAddr, Load, or_1_out, or_2_out, While_q,
       WriteEnd;
  wire [3:0] counter_1_q;
  wire [31:0] CurrentAddress_q;

  Counter #(.width(32), .max('hffffffff)) CurrentAddress (
    .count(IncAddr), .Q({CurrentAddress_q[31:18], Address, CurrentAddress_q[1:0]}), .clk(Clock), .clr(CLR));  // open: load, D, carry
  or or_1 (or_1_out, IncAddr, demultiplexer_3_out1, Finished);
  D_Flip_Flop IDLE (.clk(Clock), .D(or_1_out), .Q(IDLE_q), .preset(CLR));  // open: Qn, en, reset
  Demultiplexer #(.enable("false")) demultiplexer_1 (.out0(Load), .out1(Finished), .in(IDLE_q), .sel(End));
  D_Flip_Flop While (.clk(Clock), .D(or_2_out), .Q(While_q), .reset(CLR));  // open: Qn, preset, en
  or or_2 (or_2_out, Write, Load);
  RAM_part #(.addrWidth(18), .dataWidth(32)) ram_1 (
    .addr({Address, CurrentAddress_q[1:0]}), .data(Data), .clk(Clock));  // open: sel, ld, clr
  Demultiplexer #(.enable("false")) demultiplexer_2 (
    .out0(Write), .out1(demultiplexer_2_out1), .in(While_q), .sel(WriteEnd));
  Decoder #(.select(2)) decoder_1 (
    .out0(Mask[0]), .out1(Mask[1]), .out2(Mask[2]), .out3(Mask[3]), .sel(CurrentAddress_q[1:0]));  // open: en
  Demultiplexer #(.enable("false")) demultiplexer_3 (
    .out0(IncAddr), .out1(demultiplexer_3_out1), .in(demultiplexer_2_out1), .sel(End));
  Counter #(.width(4), .max('hf)) counter_1 (
    .load(Load), .D(WriteTime), .count(Write), .Q(counter_1_q), .clk(Clock));  // open: carry, clr
  Comparator #(.width(32)) comparator_1 (.a(Data), .b({32{1'b1}}), .eq(End));  // open: gt, lt
  Comparator #(.width(4)) comparator_2 (.a(4'b0000), .b(counter_1_q), .eq(WriteEnd));  // open: gt, lt

  // Other names for the same wires on the sheet: CLK = Clock; Count = Write; WT[3:0] = WriteTime
endmodule
